# Fritzing sketch Alchemist (saved by Fritzing 0.9.10b)
circuit board: 7cm x 2.9cm
breadboards: 1

parts:
  M2 = Stepper Motor - Bipolar
  DRV_1 = DRV 8825 Stepper Motor Carrier, High Current [part_number="DRV 8825"]
  Part1 = Arduino Nano (Rev3.0)
  lid_button = Pushbutton [package="[THT]"]
  limit_button = Pushbutton [package="[THT]"]
  5V = Power plug
  12V = Power plug
  R1 = Resistor [tolerance=±5% power=0.25 resistance=1000 package=THT]
  C2 = Electrolytic Capacitor [capacitance=100µF voltage=35V package="100 mil [THT, electrolytic]"]
  lock_placeholder = Basic Servo
  Q1 = NPN-Transistor [package="TO92 [THT]"]
  npn_pulldown = Resistor [tolerance=±5% power=0.25 resistance=10000 package=THT]
  Part2 = RFID-RC522-v2
  Part3 = RFID-RC522-v2

nets (from the schematic view):
  N1: M2.A, DRV_1.OUT_2B
  N2: M2.C, DRV_1.OUT_2A
  N3: M2.B, DRV_1.OUT_1A
  N4: M2.D, DRV_1.OUT_1B
  N5: DRV_1.ENABLE, Part1.D6
  3.3V: DRV_1.RESET, DRV_1.SLEEP, Part1.VIN, 5V.VCC, Part2.3.3V, Part3.3.3V
  N6: DRV_1.STEP, Part1.D3
  N7: DRV_1.DIRECTION, Part1.D2
  N8: DRV_1.VOLTAGE_ST/_MT, 12V.VCC, C2.+, Q1.C
  GND: DRV_1.GROUND_ST/_MT, 12V.GND, C2.-, lock_placeholder.gnd
  GND_2: Part1.GND, lid_button.Pin_1, lid_button.Pin_2, limit_button.Pin_2, 5V.GND, npn_pulldown.Pin_0, Part2.GND
  N9: Part1.D4, lid_button.Pin_3, lid_button.Pin_4
  N10: Part1.D5, limit_button.Pin_4
  N11: Part1.D7, R1.Pin_0, npn_pulldown.Pin_1
  N12: Part1.D8, Part2.SDA
  N13: Part1.D9, Part3.SDA
  N14: Part1.D10, Part3.RST
  N15: Part1.D11/MOSI, Part2.MOSI, Part3.MOSI
  N16: Part1.D12/MISO, Part2.MISO, Part3.MISO
  N17: Part1.D13/SCK, Part2.SCK, Part3.SCK
  N18: R1.Pin_1, Q1.B
  N19: lock_placeholder.vcc, Q1.E

custom parts:
  RFID-RC522-v2: A simple China made RFID-RC522 Reader; do check the pin labels, as this is a MFRC522 based clone.
