# Fritzing sketch Cabin Door_v2 (saved by Fritzing 0.9.10b)
perfboards: 1

parts:
  Part1 = Arduino Nano (Rev3.0)
  12_Volt_input = Power plug
  U1 = HALL-EFFECT [package=sc70]
  U2 = HALL-EFFECT [package=sc70]
  U3 = HALL-EFFECT [package=sc70]
  U4 = HALL-EFFECT [package=sc70]
  M1 = RioRand LM2596
  Placeholder_keybox_Lock = DC Motor [voltage_(max)=6V voltage_(min)=3V]
  Placeholder_door_Lock = DC Motor [voltage_(max)=6V voltage_(min)=3V]
  placholder_for_simple_relay_shield = WeMos D1 Mini Relay Shield V2
  trans_base = Resistor [tolerance=±5% power=0.25 resistance=1k package=THT]
  maglock_diode = Schottky Diode [part_number=1N5817 package="Melf DO-213 AB [SMD]"]  # not connected
  Ethernet_card = ENC28J60 [package=ssop28db]
  S2 = Pushbutton [package="[SMD]"]
  light_in_keybox = LEDs [package=led-1206]
  J1 = Camdenboss CTB0158-3 [part_number=CTB0158-3 package=THT]
  J2 = Camdenboss CTB0158-3 [part_number=CTB0158-3 package=THT]
  J3 = Camdenboss CTB0158-3 [part_number=CTB0158-3 package=THT]
  J4 = Camdenboss CTB0158-3 [part_number=CTB0158-3 package=THT]
  R2 = Resistor [tolerance=±5% power=0.25 resistance=220 package=THT]
  transistor_pull_down = Resistor [tolerance=±5% power=0.25 resistance=10k package=THT]
  Q2 = npn-Powertransistor [package="TO220 [THT]"]

nets (from the breadboard view):
  N1: Part1.RESET, Ethernet_card.RESET
  N2: Part1.GND, Part1.D2, placholder_for_simple_relay_shield.G, Ethernet_card.TPIN-, S2.Pin_3, S2.Pin_4
  N3: Part1.D3, placholder_for_simple_relay_shield.D4
  N4: Part1.D4, J4.pin3
  N5: Part1.D5, J4.pin2
  N6: Part1.D6, J4.pin1
  N7: Part1.D7, J3.pin3
  N8: Part1.D8, trans_base.Pin_1, transistor_pull_down.Pin_1
  N9: Part1.D10, Ethernet_card.CS
  N10: Part1.D11/MOSI, Ethernet_card.NC
  N11: Part1.D12/MISO, Ethernet_card._INT
  VIN: Part1.VIN, M1.Pin_3, placholder_for_simple_relay_shield.5V, Ethernet_card.TPIN+, J2.pin2
  N12: 12_Volt_input.GND, M1.Pin_2, Placeholder_door_Lock.pin_2, Q2.base
  N13: 12_Volt_input.VCC, M1.Pin_1, Placeholder_keybox_Lock.pin_1, placholder_for_simple_relay_shield.NO, light_in_keybox.A
  N14: U1.GND, J1.terminal_1
  N15: U1.VCC, J3.terminal_3
  N16: U1.OUT, J2.terminal_2
  N17: U2.GND, J1.terminal_2
  N18: U2.VCC, J4.terminal_1
  N19: U2.OUT, J2.terminal_3
  N20: U3.GND, J1.terminal_3
  N21: U3.VCC, J4.terminal_2
  N22: U3.OUT, J3.terminal_1
  N23: U4.GND, J2.terminal_1
  N24: U4.VCC, J4.terminal_3
  N25: U4.OUT, J3.terminal_2
  N26: Placeholder_keybox_Lock.pin_2, R2.Pin_0, Q2.collector
  N27: Placeholder_door_Lock.pin_1, placholder_for_simple_relay_shield.COM
  N28: trans_base.Pin_0, Q2.emitter
  N29: S2.Pin_1, S2.Pin_2
  N30: light_in_keybox.C, R2.Pin_1
  N31: J1.pin1, J2.pin1
