# Fritzing sketch CageLock (saved by Fritzing 0.9.10b)
breadboards: 1

parts:
  12_V = Power plug
  5V_relay = KY-019 5V Relay Module [package="Breakout board"]
  maglock = DC Motor [voltage_(max)=6V voltage_(min)=3V]
  Buttons = SWITCH-MOMENTARY-2 [package=tactile_switch_tall]
  R1 = Resistor [tolerance=±5% power=0.25 resistance=1.5k package=THT]
  R2 = Resistor [tolerance=±5% power=0.25 resistance=1k package=THT]
  D1 = Rectifier Diode [part_number=1N4001 package="300 mil [THT]"]
  12_V1 = Power plug
  5V_relay1 = KY-019 5V Relay Module [package="Breakout board"]
  maglock1 = DC Motor [voltage_(max)=6V voltage_(min)=3V]
  Buttons1 = SWITCH-MOMENTARY-2 [package=tactile_switch_tall]
  R3 = Resistor [tolerance=±5% power=0.25 resistance=1.5k package=THT]
  R4 = Resistor [tolerance=±5% power=0.25 resistance=1k package=THT]
  D2 = Rectifier Diode [part_number=1N4001 package="300 mil [THT]"]
  R5 = Resistor [tolerance=±5% power=0.25 resistance=1.5k package=THT]
  R6 = Resistor [tolerance=±5% power=0.25 resistance=1k package=THT]

nets:
  N1: 12_V.GND, 5V_relay.-, maglock.pin_2, R2.Pin_0, D1.anode
  N2: 12_V.VCC, 5V_relay.Common, R1.Pin_1
  N3: 5V_relay.S, Buttons.2
  N4: 5V_relay.+, Buttons.1, R1.Pin_0, R2.Pin_1
  N5: 5V_relay.NC, maglock.pin_1, D1.cathode
  N6: 12_V1.GND, 5V_relay1.-, maglock1.pin_2, R4.Pin_0, D2.anode, R6.Pin_0
  N7: 12_V1.VCC, 5V_relay1.Common, R3.Pin_1, R5.Pin_1
  N8: 5V_relay1.S, Buttons1.2
  N9: 5V_relay1.+, R3.Pin_0, R4.Pin_1
  N10: 5V_relay1.NC, maglock1.pin_1, D2.cathode
  N11: Buttons1.1, R5.Pin_0, R6.Pin_1

custom parts:
  KY-019 5V Relay Module: KY-019 5V Relay module, used to control AC circuits. (Special thanks to vanepp for fixing the PCB holes and other errors)
