# Fritzing sketch CageLock_v2 (saved by Fritzing 0.9.10b)

parts:
  12_V = Power plug
  D1 = Rectifier Diode [part_number=1N4001 package="300 mil [THT]"]
  A1 = uhppote electric strike door lock
  S1 = Pushbutton [package="[THT]"]
  S3 = Pushbutton [package="[THT]"]

nets (from the breadboard view):
  N1: 12_V.GND, D1.anode, A1.pin1
  N2: 12_V.VCC, D1.cathode, A1.pin2, S1.Pin_1, S1.Pin_2, S3.Pin_1, S3.Pin_2
  N3: S1.Pin_3, S1.Pin_4

custom parts:
  uhppote electric strike door lock: UHPPOTE electric strike door lock.
