# Fritzing sketch Herbs_R2 (saved by Fritzing 1.0.3b)
breadboards: 1

parts:
  Part1 = Arduino Uno (Rev3) - ICSP
  U4 = RELAY [package=relay-g5q]
  BC547 = NPN-Transistor [package="TO92 [THT]"]
  D1 = Rectifier Diode [part_number=1N4007 package="300 mil [THT]"]
  hw-178_multiplexer = Analog Digital MUX Breakout
  R1 = Resistor [tolerance=±5% power=0.25W resistance=1k package=THT]
  12V = Power plug
  Magnetic_Lock = DC Motor [voltage_(max)=6V voltage_(min)=3V]
  C1 = Ceramic Capacitor [capacitance=100nF voltage=12V package="100 mil [THT, multilayer]"]
  C2 = Electrolytic Capacitor [capacitance=1µF voltage=35V package="100 mil [THT, electrolytic]"]
  5v_output = Voltage Regulator - Variable [package="TO220 [THT]"]
  R2 = Resistor [tolerance=±5% power=0.25W resistance=330 package=THT]
  R3 = Resistor [tolerance=±5% power=0.25W resistance=1k package=THT]
  COM-TTL-RS485_placeholder = 24LC01 [package=THT]
  S1 = SWITCH-MOMENTARY-2 [package=reed_switch_pth]
  S2 = SWITCH-MOMENTARY-2 [package=reed_switch_pth]
  S4 = SWITCH-MOMENTARY-2 [package=reed_switch_pth]
  S3 = SWITCH-MOMENTARY-2 [package=reed_switch_pth]
  S6 = SWITCH-MOMENTARY-2 [package=reed_switch_pth]
  S7 = SWITCH-MOMENTARY-2 [package=reed_switch_pth]
  S8 = SWITCH-MOMENTARY-2 [package=reed_switch_pth]
  S5 = SWITCH-MOMENTARY-2 [package=reed_switch_pth]
  S10 = SWITCH-MOMENTARY-2 [package=reed_switch_pth]
  S9 = SWITCH-MOMENTARY-2 [package=reed_switch_pth]

nets:
  GND: Part1.GND, U4.NO, BC547.E, hw-178_multiplexer.GND, hw-178_multiplexer.EN, R1.Pin_0, 12V.GND, C1.0, C2.-, COM-TTL-RS485_placeholder.0V, S1.2, S2.2, S4.2, S3.2, S6.2, S7.2, S8.2, S5.2, S10.2, S9.2
  N1: Part1.D10_PWM/SS, R3.Pin_0
  N2: Part1.D0/RX, COM-TTL-RS485_placeholder.A2
  N3: Part1.D1/TX, COM-TTL-RS485_placeholder.A1
  N4: Part1.D2, hw-178_multiplexer.SIG
  N5: Part1.D3_PWM, hw-178_multiplexer.S0
  N6: Part1.D4, hw-178_multiplexer.S1
  N7: Part1.D5_PWM, hw-178_multiplexer.S2
  N8: Part1.D6_PWM, hw-178_multiplexer.S3
  VIN: Part1.VIN, 12V.VCC, Magnetic_Lock.pin_1, C1.1, 5v_output.IN
  N9: U4.COIL2, BC547.C, D1.anode
  N10: U4.MAIN, Magnetic_Lock.pin_2
  N11: U4.COIL1, D1.cathode, hw-178_multiplexer.VCC, C2.+, 5v_output.OUT, R2.Pin_1, COM-TTL-RS485_placeholder.A0
  N12: BC547.B, R3.Pin_1
  N13: hw-178_multiplexer.C0, S10.1
  N14: hw-178_multiplexer.C1, S9.1
  N15: hw-178_multiplexer.C2, S8.1
  N16: hw-178_multiplexer.C3, S7.1
  N17: hw-178_multiplexer.C4, S6.1
  N18: hw-178_multiplexer.C5, S5.1
  N19: hw-178_multiplexer.C6, S4.1
  N20: hw-178_multiplexer.C7, S3.1
  N21: hw-178_multiplexer.C8, S2.1
  N22: hw-178_multiplexer.C9, S1.1
  N23: R1.Pin_1, 5v_output.ADJ, R2.Pin_0
  Ground: COM-TTL-RS485_placeholder.SCL_-_I2C_Clock
  B: COM-TTL-RS485_placeholder.WP_-_Write_Protect
  A: COM-TTL-RS485_placeholder.+V
