# Fritzing sketch Herbs_R2_02 (saved by Fritzing 1.0.3b)
breadboards: 1

parts:
  part = Arduino Uno (Rev3) - ICSP
  Relay = RELAY [package=relay-g5q]
  BC547 = NPN-Transistor [package="TO92 [THT]"]
  D1 = Rectifier Diode [part_number=1N4007 package="300 mil [THT]"]
  hw-178_multiplexer = Analog Digital MUX Breakout
  12V = Power plug
  Magnetic_Lock = DC Motor [voltage_(max)=6V voltage_(min)=3V]
  R3 = Resistor [tolerance=±5% power=0.25W resistance=1k package=THT]
  COM-TTL-RS485_placeholder = 24LC01 [package=THT]
  S1 = SWITCH-MOMENTARY-2 [package=reed_switch_pth]
  S2 = SWITCH-MOMENTARY-2 [package=reed_switch_pth]
  S4 = SWITCH-MOMENTARY-2 [package=reed_switch_pth]
  S3 = SWITCH-MOMENTARY-2 [package=reed_switch_pth]
  S6 = SWITCH-MOMENTARY-2 [package=reed_switch_pth]
  S7 = SWITCH-MOMENTARY-2 [package=reed_switch_pth]
  S8 = SWITCH-MOMENTARY-2 [package=reed_switch_pth]
  S5 = SWITCH-MOMENTARY-2 [package=reed_switch_pth]
  S10 = SWITCH-MOMENTARY-2 [package=reed_switch_pth]
  S9 = SWITCH-MOMENTARY-2 [package=reed_switch_pth]
  LED_power_out = Hirose DF13 Series Header [part_number=DF13A-2P-1.25H package=DF13A-2P-1.25H]
  Serial_RX_on/off = SWITCH-MOMENTARY-2 [package=tactile-switch-1101ne]

nets:
  5V: part.5V, Relay.COIL1, D1.cathode, hw-178_multiplexer.VCC, COM-TTL-RS485_placeholder.A0
  GND: part.GND, BC547.E, hw-178_multiplexer.GND, hw-178_multiplexer.EN, 12V.GND, Magnetic_Lock.pin_1, COM-TTL-RS485_placeholder.0V, S1.2, S2.2, S4.2, S3.2, S6.2, S7.2, S8.2, S5.2, S10.2, S9.2, LED_power_out.1
  N1: part.D10_PWM/SS, R3.Pin_0
  N2: part.D0/RX, Serial_RX_on/off.2
  N3: part.D1/TX, COM-TTL-RS485_placeholder.A1
  N4: part.D2, hw-178_multiplexer.S0
  N5: part.D3_PWM, hw-178_multiplexer.S1
  N6: part.D4, hw-178_multiplexer.S2
  N7: part.D5_PWM, hw-178_multiplexer.S3
  N8: part.D6_PWM, hw-178_multiplexer.SIG
  VIN: part.VIN, Relay.MAIN, 12V.VCC, LED_power_out.2
  N9: Relay.COIL2, BC547.C, D1.anode
  N10: Relay.NO, Magnetic_Lock.pin_2
  N11: BC547.B, R3.Pin_1
  N12: hw-178_multiplexer.C0, S10.1
  N13: hw-178_multiplexer.C1, S9.1
  N14: hw-178_multiplexer.C2, S8.1
  N15: hw-178_multiplexer.C3, S7.1
  N16: hw-178_multiplexer.C4, S6.1
  N17: hw-178_multiplexer.C5, S5.1
  N18: hw-178_multiplexer.C6, S4.1
  N19: hw-178_multiplexer.C7, S3.1
  N20: hw-178_multiplexer.C8, S2.1
  N21: hw-178_multiplexer.C9, S1.1
  N22: COM-TTL-RS485_placeholder.A2, Serial_RX_on/off.1
  Ground: COM-TTL-RS485_placeholder.SCL_-_I2C_Clock
  B: COM-TTL-RS485_placeholder.WP_-_Write_Protect
  A: COM-TTL-RS485_placeholder.+V

notes:
  Reed switches connected via repurposed SCART cable
  Toggle switch to break RX connection for code upload
  connected via screw terminal
