# Fritzing sketch KnockKnock (saved by Fritzing 0.9.10b)
breadboards: 1

parts:
  Mod1 = Amica NodeMCU DEVKIT 1.0
  M1 = DC Motor [voltage_(max)=6V voltage_(min)=3V]
  M2 = DC Motor [voltage_(max)=6V voltage_(min)=3V]
  12V = Power plug
  M3 = RioRand LM2596
  Mod2 = KY-019 5V Relay Module [package="Breakout board"]

nets:
  N1: Mod1.pin1, Mod1.pin_10, Mod1.pin_26
  N2: Mod1.pin2, Mod1.pin_9, Mod1.pin_25, Mod1.pin_29
  N3: Mod1.pin_15, Mod2.S
  N4: M1.pin_1, M2.pin_1, 12V.VCC, M3.Pin_1
  N5: M1.pin_2, M2.pin_2, Mod2.NC
  N6: 12V.GND, M3.Pin_2, Mod2.Common
  N7: M3.Pin_3, Mod2.+
  N8: M3.Pin_4, Mod2.-

custom parts:
  KY-019 5V Relay Module: KY-019 5V Relay module, used to control AC circuits. (Special thanks to vanepp for fixing the PCB holes and other errors)
