# Fritzing sketch KnockKnock_recover (saved by Fritzing 0.9.10b)
breadboards: 1

parts:
  lock_3 = DC Motor [voltage_(max)=6V voltage_(min)=3V]
  lock_2 = DC Motor [voltage_(max)=6V voltage_(min)=3V]
  12V = Power plug
  step_down_to_5V = RioRand LM2596
  relay = KY-019 5V Relay Module [package="Breakout board"]
  nano = Arduino Nano (Rev3.0) (ICSP)
  piezo = Piezo Speaker
  D1 = Rectifier Diode [part_number=1N4001 package="300 mil [THT]"]
  R1 = Resistor [tolerance=±5% power=0.25 resistance=220 package=THT]
  12V_2 = Power plug

nets:
  N1: lock_3.pin_1, lock_2.pin_1, 12V.VCC
  N2: lock_3.pin_2, lock_2.pin_2, relay.NC
  N3: 12V.GND, relay.Common
  N4: step_down_to_5V.Pin_1, 12V_2.VCC
  N5: step_down_to_5V.Pin_2, 12V_2.GND
  N6: step_down_to_5V.Pin_3, relay.+, nano.VIN
  N7: step_down_to_5V.Pin_4, relay.-, nano.GND, piezo.pin1, D1.anode, R1.Pin_0
  N8: relay.S, nano.D12/MISO
  N9: nano.A0, piezo.pin2, D1.cathode, R1.Pin_1

custom parts:
  KY-019 5V Relay Module: KY-019 5V Relay module, used to control AC circuits. (Special thanks to vanepp for fixing the PCB holes and other errors)
