# Fritzing sketch RuneWall (saved by Fritzing 0.9.10b)
breadboards: 1

parts:
  R2 = Resistor [tolerance=±5% power=0.25 resistance=1M package=THT]
  U1 = Barometric Pressure Sensor
  Part1 = Arduino Nano (Rev3.0)
  Power_plug1 = Power plug
  Q1 = NPN-Transistor [package="TO92 [THT]"]
  R3 = Resistor [tolerance=±5% power=0.25 resistance=220 package=THT]
  Rg = Resistor [tolerance=±5% power=0.25 resistance=220 package=THT]
  Rb = Resistor [tolerance=±5% power=0.25 resistance=220 package=THT]
  LED = RGB LED - (4 legs) [package="5 mm [THT]"]
  Rr = Resistor [tolerance=±5% power=0.25 resistance=220 package=THT]

nets (from the schematic view):
  N1: R2.Pin_1, U1.GND, Part1.D9
  VIN: Part1.VIN, Power_plug1.VCC, LED.common_anode
  GND: Part1.GND, Power_plug1.GND, Q1.E, Rr.Pin_0
  N2: Part1.A0, R3.Pin_0
  N3: Q1.B, R3.Pin_1
  N4: Q1.C, Rg.Pin_0, Rb.Pin_0
  N5: Rg.Pin_1, LED.green_cathode
  N6: Rb.Pin_1, LED.blue_cathode
  N7: LED.red_cathode, Rr.Pin_1
