# Fritzing sketch RuneWall_recover (saved by Fritzing 0.9.10b)
breadboards: 1

parts:
  R2 = Resistor [tolerance=±5% power=0.25 resistance=4.7M package=THT]
  Part1 = Arduino Nano (Rev3.0)
  5V = Power plug
  Q1 = NPN-Transistor [package="TO92 [THT]"]
  R3 = Resistor [tolerance=±5% power=0.25 resistance=220 package=THT]
  Rg = Resistor [tolerance=±5% power=0.25 resistance=220 package=THT]
  Rb = Resistor [tolerance=±5% power=0.25 resistance=220 package=THT]
  LED = RGB LED - (4 legs) [package="5 mm [THT]"]
  Rr = Resistor [tolerance=±5% power=0.25 resistance=220 package=THT]
  capacitive_metal_1 = Screw terminal - 2 pins [package=THT]
  adafruit_capacitive_board_placeholder = JeePlug experimenter's board  # not connected
  12V = Power plug
  R4 = Resistor [tolerance=±5% power=0.25 resistance=220 package=THT]
  Q2 = NPN-Transistor [package="TO92 [THT]"]
  R5 = Resistor [tolerance=±5% power=0.25 resistance=220 package=THT]
  R6 = Resistor [tolerance=±5% power=0.25 resistance=220 package=THT]
  LED1 = RGB LED - (4 legs) [package="5 mm [THT]"]
  Rr1 = Resistor [tolerance=±5% power=0.25 resistance=220 package=THT]
  Rg1 = Resistor [tolerance=±5% power=0.25 resistance=220 package=THT]
  Rb1 = Resistor [tolerance=±5% power=0.25 resistance=220 package=THT]
  Q3 = NPN-Transistor [package="TO92 [THT]"]
  R7 = Resistor [tolerance=±5% power=0.25 resistance=220 package=THT]
  R8 = Resistor [tolerance=±5% power=0.25 resistance=220 package=THT]
  LED2 = RGB LED - (4 legs) [package="5 mm [THT]"]
  Rr2 = Resistor [tolerance=±5% power=0.25 resistance=220 package=THT]
  Rg2 = Resistor [tolerance=±5% power=0.25 resistance=220 package=THT]
  Rb2 = Resistor [tolerance=±5% power=0.25 resistance=220 package=THT]

nets (from the schematic view):
  N1: R2.Pin_0, Part1.D2
  N2: R2.Pin_1, Part1.D3, capacitive_metal_1.pin1
  GND: Part1.GND, 5V.GND, Q1.E, Rr.Pin_0, R4.Pin_0
  N3: Part1.D8, R7.Pin_0
  N4: Part1.D9, R5.Pin_0
  N5: Part1.D10, R3.Pin_0
  VIN: Part1.VIN, 5V.VCC
  N6: Q1.B, R3.Pin_1, R4.Pin_1
  N7: Q1.C, Rg.Pin_0, Rb.Pin_0
  N8: Rg.Pin_1, LED.green_cathode
  N9: Rb.Pin_1, LED.blue_cathode
  N10: LED.red_cathode, Rr.Pin_1
  N11: LED.common_anode, 12V.VCC, LED1.common_anode, LED2.common_anode
  N12: Q2.B, R5.Pin_1, R6.Pin_1
  N13: Q2.C, Rg1.Pin_0, Rb1.Pin_0
  N14: LED1.red_cathode, Rr1.Pin_1
  N15: LED1.green_cathode, Rg1.Pin_1
  N16: LED1.blue_cathode, Rb1.Pin_1
  N17: Q3.B, R7.Pin_1, R8.Pin_1
  N18: Q3.C, Rg2.Pin_0, Rb2.Pin_0
  N19: LED2.red_cathode, Rr2.Pin_1
  N20: LED2.green_cathode, Rg2.Pin_1
  N21: LED2.blue_cathode, Rb2.Pin_1
