# Fritzing sketch RuneWall_v2 (saved by Fritzing 0.9.10b)
breadboards: 1

parts:
  Part1 = Arduino Nano (Rev3.0)
  5V = Power plug
  Q1 = NPN-Transistor [package="TO92 [THT]"]
  R3 = Resistor [tolerance=±5% power=0.25 resistance=220 package=THT]
  Rg = Resistor [tolerance=±5% power=0.25 resistance=220 package=THT]
  Rb = Resistor [tolerance=±5% power=0.25 resistance=220 package=THT]
  LED = RGB LED - (4 legs) [package="5 mm [THT]"]
  Rr = Resistor [tolerance=±5% power=0.25 resistance=220 package=THT]
  capacitive_metal_1 = Screw terminal - 2 pins [package=THT]
  adafruit_capacitive_board_placeholder = JeePlug experimenter's board
  12V = Power plug
  R4 = Resistor [tolerance=±5% power=0.25 resistance=220 package=THT]
  Q2 = NPN-Transistor [package="TO92 [THT]"]
  R5 = Resistor [tolerance=±5% power=0.25 resistance=220 package=THT]
  R6 = Resistor [tolerance=±5% power=0.25 resistance=220 package=THT]
  LED1 = RGB LED - (4 legs) [package="5 mm [THT]"]
  Rr1 = Resistor [tolerance=±5% power=0.25 resistance=220 package=THT]
  Rg1 = Resistor [tolerance=±5% power=0.25 resistance=220 package=THT]
  Rb1 = Resistor [tolerance=±5% power=0.25 resistance=220 package=THT]
  Q3 = NPN-Transistor [package="TO92 [THT]"]
  R7 = Resistor [tolerance=±5% power=0.25 resistance=220 package=THT]
  R8 = Resistor [tolerance=±5% power=0.25 resistance=220 package=THT]
  LED2 = RGB LED - (4 legs) [package="5 mm [THT]"]
  Rr2 = Resistor [tolerance=±5% power=0.25 resistance=220 package=THT]
  Rg2 = Resistor [tolerance=±5% power=0.25 resistance=220 package=THT]
  Rb2 = Resistor [tolerance=±5% power=0.25 resistance=220 package=THT]
  capacitive_metal_2 = Screw terminal - 2 pins [package=THT]
  capacitive_metal_3 = Screw terminal - 2 pins [package=THT]
  maglock = DC Motor [voltage_(max)=6V voltage_(min)=3V]
  D1 = Rectifier Diode [part_number=1N4001 package="300 mil [THT]"]
  Mod1 = KY-019 5V Relay Module [package="Breakout board"]

nets (from the schematic view):
  N1: Part1.D3, Mod1.S
  rune 10: Part1.D4
  rune 09: Part1.D5
  rune 08: Part1.D6
  rune 07: Part1.D7
  rune 06: Part1.D8
  rune 05: Part1.D9
  rune 04: Part1.D10
  N2: Part1.D11/MOSI, R7.Pin_0
  N3: Part1.D12/MISO, R5.Pin_0
  VIN: Part1.VIN, 5V.VCC, Mod1.+
  GND: Part1.GND, 5V.GND, Mod1.-
  N4: Part1.A5, adafruit_capacitive_board_placeholder.A2
  N5: Part1.A4, adafruit_capacitive_board_placeholder.A1
  N6: Part1.D13/SCK, R3.Pin_0
  N7: Q1.B, R3.Pin_1, R4.Pin_1
  N8: Q1.C, Rg.Pin_0, Rb.Pin_0
  N9: Rg.Pin_1, LED.green_cathode
  N10: Rb.Pin_1, LED.blue_cathode
  N11: LED.red_cathode, Rr.Pin_1
  N12: LED.common_anode, 12V.VCC, LED1.common_anode, LED2.common_anode, Mod1.Common
  N13: Rr.Pin_0, Q2.E, R6.Pin_0, Rr1.Pin_0, Q3.E, R8.Pin_0, Rr2.Pin_0, maglock.pin_2, D1.anode
  N14: capacitive_metal_1.pin1, adafruit_capacitive_board_placeholder.B1
  N15: adafruit_capacitive_board_placeholder.B3, capacitive_metal_3.pin1
  N16: adafruit_capacitive_board_placeholder.B2, capacitive_metal_2.pin1
  N17: 12V.GND, R4.Pin_0
  N18: Q2.B, R5.Pin_1, R6.Pin_1
  N19: Q2.C, Rg1.Pin_0, Rb1.Pin_0
  N20: LED1.red_cathode, Rr1.Pin_1
  N21: LED1.green_cathode, Rg1.Pin_1
  N22: LED1.blue_cathode, Rb1.Pin_1
  N23: Q3.B, R7.Pin_1, R8.Pin_1
  N24: Q3.C, Rg2.Pin_0, Rb2.Pin_0
  N25: LED2.red_cathode, Rr2.Pin_1
  N26: LED2.green_cathode, Rg2.Pin_1
  N27: LED2.blue_cathode, Rb2.Pin_1
  N28: maglock.pin_1, D1.cathode, Mod1.NC

custom parts:
  KY-019 5V Relay Module: KY-019 5V Relay module, used to control AC circuits. (Special thanks to vanepp for fixing the PCB holes and other errors)
