# Fritzing sketch SmokeMachine remote (saved by Fritzing 0.9.3b)
breadboards: 1

parts:
  R1 = Resistor [tolerance=±5% resistance=220 package=THT]
  R2 = Resistor [tolerance=±5% resistance=220 package=THT]
  D1 = Rectifier Diode [part_number=1N4001 package="300 mil [THT]"]
  D2 = Rectifier Diode [part_number=1N4001 package="300 mil [THT]"]
  S2 = Pushbutton [package=THT]
  Groene_LED = LED - 5mm [color="Green (570nm)" package="5 mm [THT]"]
  LED2 = LED - 5mm [color="Red (633nm)" package="5 mm [THT]"]

nets:
  N1: R1.Pin_0, Groene_LED.cathode
  Zwart: R1.Pin_1, R2.Pin_1, D2.cathode, S2.leg0
  N2: R2.Pin_0, LED2.anode
  Bruin: D1.cathode, S2.leg1
  N3: D1.anode, D2.anode, LED2.cathode
  Blauw: Groene_LED.anode

notes:
  Zwart+Bruin = rode led
  Zwart+Blauw = groene led (?)
