# Fritzing sketch potions (saved by Fritzing 0.9.10b)
breadboards: 1

parts:
  MIC = Breakout Board for Electret Microphone
  M1 = DC Motor [voltage_(max)=3V voltage_(min)=1.5V]
  M2 = DC Motor [voltage_(max)=3V voltage_(min)=1.5V]
  M4 = DC Motor [voltage_(max)=3V voltage_(min)=1.5V]
  M3 = DC Motor [voltage_(max)=3V voltage_(min)=1.5V]
  Part2 = Arduino Nano (Rev3.0)
  LED1 = smd LED [color="Red (633nm)" package="0805 [SMD]"]
  1_5_V = Power plug
  5V = Power plug
  led1_r = Resistor [tolerance=±5% power=0.25 resistance=220 package=THT]
  relay = KY-019 5V Relay Module [package="Breakout board"]
  LED4 = smd LED [color="Red (633nm)" package="0805 [SMD]"]
  R1 = Rotary Potentiometer (Small) [maximum_resistance=100kΩ knob_status=50% power=0.5W package=THT]  # not connected

nets (from the schematic view):
  VCC: MIC.VCC, Part2.VIN, 5V.VCC, relay.+
  GND: MIC.GND, Part2.GND, 5V.GND, relay.-
  N1: MIC.AUD, Part2.D9
  N2: M1.pin_1, M2.pin_1, M4.pin_1, M3.pin_1, 1_5_V.VCC
  N3: M1.pin_2, M2.pin_2, M4.pin_2, M3.pin_2, relay.Common
  N4: Part2.A3, relay.S
  N5: LED1.cathode, LED4.anode
  N6: LED1.anode, led1_r.Pin_1
  N7: 1_5_V.GND, relay.NC

custom parts:
  KY-019 5V Relay Module: KY-019 5V Relay module, used to control AC circuits. (Special thanks to vanepp for fixing the PCB holes and other errors)
