# Fritzing sketch potions_recover (saved by Fritzing 0.9.10b)
breadboards: 1

parts:
  MIC = Breakout Board for Electret Microphone
  M1 = DC Motor [voltage_(max)=3V voltage_(min)=1.5V]
  M2 = DC Motor [voltage_(max)=3V voltage_(min)=1.5V]
  M4 = DC Motor [voltage_(max)=3V voltage_(min)=1.5V]
  M3 = DC Motor [voltage_(max)=3V voltage_(min)=1.5V]
  Part2 = Arduino Nano (Rev3.0)
  1_5_V = Power plug
  5V = Power plug
  relay = KY-019 5V Relay Module [package="Breakout board"]
  R1 = Rotary Potentiometer (Small) [maximum_resistance=100kΩ knob_status=50% power=0.5W package=THT]  # not connected
  relay1 = KY-019 5V Relay Module [package="Breakout board"]
  Part3 = Arduino Nano (Rev3.0)
  1_5_V1 = Power plug
  R2 = Resistor [tolerance=±5% power=0.25 resistance=220 package=THT]

nets (from the schematic view):
  VCC: MIC.VCC, Part2.VIN, 5V.VCC, relay.+
  GND: MIC.GND, Part2.GND, 5V.GND, relay.-
  N1: MIC.AUD, Part2.D9
  N2: M1.pin_1, M2.pin_1, M4.pin_1, M3.pin_1, 1_5_V.VCC
  N3: M1.pin_2, M2.pin_2, M4.pin_2, M3.pin_2, relay.Common
  N4: Part2.A1, relay.S
  N5: 1_5_V.GND, relay.NC
  N6: relay1.S, Part3.D1/TX, R2.Pin_0
  VIN: relay1.+, Part3.VIN, 1_5_V1.VCC, R2.Pin_1
  GND_2: relay1.-, Part3.GND, 1_5_V1.GND

custom parts:
  KY-019 5V Relay Module: KY-019 5V Relay module, used to control AC circuits. (Special thanks to vanepp for fixing the PCB holes and other errors)
