# Fritzing sketch runeWall_LED (saved by Fritzing 0.9.10b)
circuit board: 20.3126cm x 4.64417cm
breadboards: 2

parts:
  Q1 = NPN-Transistor [package="SOT-23 [SMD]"]
  Part1 = Arduino Nano (Rev3.0) (ICSP)
  12V = Power plug
  LED1 = LED - 3mm [color="Red (633nm)" current=0.030 package="3 mm [THT]"]
  R1 = Resistor [tolerance=±5% power=0.25 resistance=220 package=THT]
  5V = Power plug
  Q2 = NPN-Transistor [package="SOT-23 [SMD]"]
  Part2 = Arduino Nano (Rev3.0) (ICSP)
  12V1 = Power plug
  R2 = Resistor [tolerance=±5% power=0.25 resistance=220 package=THT]
  5V1 = Power plug
  LED3 = RGB LED (com. anode, rbg) [package="5 mm [THT]"]
  R3 = Resistor [tolerance=±5% power=0.25 resistance=240 package=THT]
  R4 = Resistor [tolerance=±5% power=0.25 resistance=470 package=THT]
  R5 = Resistor [tolerance=±5% power=0.25 resistance=240 package=THT]
  B = LED - 5mm [color="Blue (525nm)" current=0.030 package="5 mm [THT]"]
  R = LED - 5mm [color="Red (633nm)" current=0.030 package="5 mm [THT]"]
  G = LED - 5mm [color="Yellow (595nm)" current=0.030 package="5 mm [THT]"]
  R7 = LED - 5mm [color="Red (633nm)" current=0.030 package="5 mm [THT]"]
  G2 = LED - 5mm [color="Yellow (595nm)" current=0.030 package="5 mm [THT]"]
  B2 = LED - 5mm [color="Blue (525nm)" current=0.030 package="5 mm [THT]"]
  R8 = LED - 5mm [color="Red (633nm)" current=0.030 package="5 mm [THT]"]
  G3 = LED - 5mm [color="Yellow (595nm)" current=0.030 package="5 mm [THT]"]
  B3 = LED - 5mm [color="Blue (525nm)" current=0.030 package="5 mm [THT]"]
  12V_2 = Power plug

nets:
  N1: Q1.2, 12V.GND
  N2: Q1.0, R1.Pin_1
  N3: Q1.1, LED1.cathode
  GND: Part1.GND, 5V.GND
  N4: Part1.D3, R1.Pin_0
  VIN: Part1.VIN, 5V.VCC
  N5: 12V.VCC, LED1.anode
  N6: Q2.2, 12V1.GND, LED3.red_cathode
  N7: Q2.0, R2.Pin_1
  N8: Q2.1, LED3.blue_cathode, LED3.green_cathode
  GND_2: Part2.GND, 5V1.GND
  N9: Part2.D3, R2.Pin_0
  VIN_2: Part2.VIN, 5V1.VCC
  N10: 12V1.VCC, LED3.common_anode
  N11: R3.Pin_0, R.cathode
  N12: R3.Pin_1, R7.anode
  N13: R4.Pin_0, B.cathode
  N14: R4.Pin_1, B2.anode
  N15: R5.Pin_0, G2.cathode
  N16: R5.Pin_1, G3.anode
  N17: B.anode, R.anode, G.anode, 12V_2.VCC
  N18: G.cathode, G2.anode
  N19: R7.cathode, R8.anode
  N20: B2.cathode, B3.anode
  B/G/R: R8.cathode, G3.cathode, B3.cathode, 12V_2.GND

notes:
  13mA (0.013A)
  40mA (0.04A)
  per strip
